# Fritzing sketch ATM-Frits (saved by Fritzing 0.9.2b)

parts:
  Part2 = RFID-RC522-v2
  Part1 = Arduino Uno (Rev3) - ICSP
  Matrix_keypad2 = KEYPAD 4x4

nets:
  N1: Part2.SDA, Part1.D10_PWM/SS
  N2: Part2.SCK, Part1.D13/SCK
  N3: Part2.MOSI, Part1.D11_PWM/MOSI
  N4: Part2.MISO, Part1.D12/MISO
  GND: Part2.GND, Part1.GND
  N5: Part2.RST, Part1.D9_PWM
  N6: Part2.3_3V, Part1.3V3
  N7: Part1.A0, Matrix_keypad2.row1
  N8: Part1.A1, Matrix_keypad2.row2
  N9: Part1.A2, Matrix_keypad2.row3
  N10: Part1.A3, Matrix_keypad2.row4
  N11: Part1.D4, Matrix_keypad2.col4
  N12: Part1.D5_PWM, Matrix_keypad2.col3
  N13: Part1.D6_PWM, Matrix_keypad2.col2
  N14: Part1.D7, Matrix_keypad2.col1

custom parts:
  RFID-RC522-v2: A simple China made RFID-RC522 Reader; do check the pin labels, as this is a MFRC522 based clone.
  KEYPAD 4x4: Matrix keypad 16 buttons, 4 rows x 4 columns
